# Fritzing sketch pibiti (saved by Fritzing 0.9.3b)
breadboards: 1

parts:
  U1 = NodeMCU V3.0
  RTC_DS3231 = ZS-042 RTC Module
  ACS712_Sensor_de_Corrente = ACS712 Low Current Sensor Board v12
  ADC1 = MCP3008 [package=dil16]
  R1 = Resistor [tolerance=±0.05% resistance=2.5M package="2512 [SMD]"]
  Placa_Solar = SOLAR-IXYS [package=solarbit-12x1]
  R2 = Resistor [tolerance=±0.05% resistance=120k package="2512 [SMD]"]
  D1 = Rectifier Diode [part_number=1N4001 package="Melf DO-213 AB [SMD]"]
  D2 = Rectifier Diode [part_number=1N4001 package="Melf DO-213 AB [SMD]"]

nets:
  N1: U1.D1, RTC_DS3231.SCL
  N2: U1.D2, RTC_DS3231.SDA
  N3: U1.D4, ADC1.CS/SHDN
  3V3: U1.3V3, ADC1.VREF, ADC1.VDD, D1.cathode
  GND: U1.GND, RTC_DS3231.GND, ACS712_Sensor_de_Corrente.GND, ADC1.AGND, Placa_Solar.A, R2.Pin_0, D2.anode
  N4: U1.D5, ADC1.CLK
  N5: U1.D6, ADC1.Dout
  N6: U1.D7, ADC1.Din
  VIN: U1.Vin, RTC_DS3231.VCC, ACS712_Sensor_de_Corrente.5V
  N7: ACS712_Sensor_de_Corrente.IP+, Placa_Solar.C
  N8: ACS712_Sensor_de_Corrente.IP-, R1.Pin_1
  N9: ACS712_Sensor_de_Corrente.VO, ADC1.CH0
  N10: ADC1.CH1, D1.anode, D2.cathode
  N11: R1.Pin_0, R2.Pin_1

custom parts:
  NodeMCU V3.0: ESP8266 based NodeMCU
